// Logisim project IT012_Lab02_25521316.circ as structural Verilog
// FA1
module Warmup (
  input  [7:0] A,
  input  [7:0] B,
  output [7:0] out_3
);

  Adder adder_1 (.a(A), .b(B), .out(out_3));  // open: cin, cout
  // OR_Gate or_1 is placed but not wired
  // Probe on out_3
endmodule

module FA (
  input  A,
  input  B,
  input  Cin,
  output S,
  output Cout
);

  wire and_1_out, and_2_out, xor_1_out;

  and and_1 (and_1_out, A, B);
  and and_2 (and_2_out, Cin, xor_1_out);
  xor xor_1 (xor_1_out, A, B);
  or or_1 (Cout, and_1_out, and_2_out);
  xor xor_2 (S, xor_1_out, Cin);
endmodule

module ADDSUB4 (
  input  SUB,
  input  [3:0] B,
  input  [3:0] A,
  output [3:0] S,
  output N,
  output Z,
  output V,
  output C
);

  wire fa_1_cout, fa_2_cout, fa_3_cout, xor_1_out, xor_2_out, xor_3_out, xor_4_out, xor_5_out, xor_6_out;

  buf xor_1 (xor_1_out, B[0]);  // XOR_Gate
  buf xor_2 (xor_2_out, B[1]);  // XOR_Gate
  buf xor_3 (xor_3_out, B[2]);  // XOR_Gate
  buf xor_4 (xor_4_out, B[3]);  // XOR_Gate
  FA fa_1 (.A(xor_1_out), .B(A[0]), .Cin(SUB), .S(S[0]), .Cout(fa_1_cout));
  FA fa_2 (.A(xor_2_out), .B(A[1]), .Cin(fa_1_cout), .S(S[1]), .Cout(fa_2_cout));
  FA fa_3 (.A(xor_3_out), .B(A[2]), .Cin(fa_2_cout), .S(S[2]), .Cout(fa_3_cout));
  FA fa_4 (.A(xor_4_out), .B(A[3]), .Cin(fa_3_cout), .S(N), .Cout(C));
  nor nor_1 (Z, S[0], S[1], S[2], N);
  xor xor_5 (xor_5_out, B[3], N);
  xor xor_6 (xor_6_out, B[3], N);
  and and_1 (V, xor_5_out, xor_6_out);

  assign S[3] = N;
endmodule

module LT (
  input  A7,
  input  B7,
  input  R7,
  output LT
);

  wire and_1_out, and_2_out, and_3_out, not_1_out;

  not not_1 (not_1_out, B7);
  and and_1 (and_1_out, A7, not_1_out);
  and and_2 (and_2_out, A7, R7);
  and and_3 (and_3_out, not_1_out, R7);
  or or_1 (LT, and_1_out, and_2_out, and_3_out);
endmodule

module DLATCH (
  input  D,
  input  E,
  output Q
);

  Multiplexer #(.enable("false")) multiplexer_1 (.in0(Q), .in1(D), .out(Q), .sel(E));
endmodule

module DFF_MS (
  input  D,
  input  CLK,
  output Q
);

  wire dlatch_1_q, not_1_out;

  not not_1 (not_1_out, CLK);
  DLATCH dlatch_1 (.D(D), .E(not_1_out), .Q(dlatch_1_q));
  DLATCH dlatch_2 (.D(dlatch_1_q), .E(CLK), .Q(Q));
endmodule

module ALU8 (
  input  [7:0] A,
  input  [7:0] B,
  input  [2:0] OP,
  output [7:0] R,
  output Z,
  output LT
);

  wire [7:0] adder_1_out, adder_2_out, and_1_out, multiplexer_1_out, multiplexer_2_out, not_1_out,
       subtractor_1_out, subtractor_2_out;
  wire [7:1] xor_1_out;

  Adder adder_1 (.a(A), .b(B), .out(adder_1_out));  // open: cin, cout
  Adder adder_2 (.a(A), .out(adder_2_out));  // open: b, cin, cout
  Subtractor subtractor_1 (.a(A), .b(B), .out(subtractor_1_out));  // open: bin, bout
  Subtractor subtractor_2 (.a(A), .out(subtractor_2_out));  // open: b, bin, bout
  assign and_1_out = A & B;  // AND_Gate and_1, 8 bits wide
  assign and_1_out = A | B;  // OR_Gate or_1, 8 bits wide
  assign not_1_out = ~A;  // NOT_Gate not_1, 8 bits wide
  assign {xor_1_out, OP[2]} = A ^ B;  // XOR_Gate xor_1, 8 bits wide
  Multiplexer #(.select(2), .width(8), .enable("false")) multiplexer_1 (
    .in0(adder_1_out), .in1(adder_2_out), .in2(subtractor_1_out), .in3(subtractor_2_out),
    .out(multiplexer_1_out), .sel(A[1:0]));
  Multiplexer #(.select(2), .width(8), .enable("false")) multiplexer_2 (
    .in0(and_1_out), .in1(and_1_out), .in2(not_1_out), .in3({xor_1_out, OP[2]}), .out(multiplexer_2_out),
    .sel(A[1:0]));
  Multiplexer #(.width(8), .enable("false")) multiplexer_3 (
    .in0(multiplexer_1_out), .in1(multiplexer_2_out), .out({8{R[7]}}), .sel(OP[2]));
  nor nor_1 (Z, R[7], R[7], R[7], R[7], R[7], R[7], R[7], R[7]);
  LT lt_1 (.A7(A[7]), .B7(B[7]), .R7(R[7]), .LT(LT));
  // Pins of 2 and 8 bits meet at A
  // Pins of 1 and 8 bits meet at {xor_1_out, OP[2]}
  // Pins of 1 and 8 bits meet at {8{R[7]}}

  assign OP[1:0] = A[1:0];
  assign R[6:0] = {7{R[7]}};
endmodule

module TN3 (
  input  D,
  input  CLK,
  output Q1,
  output Q2,
  output Q3,
  output L1,
  output L2,
  output F1,
  output F2
);

  wire DFF_MS__master__E___CLK_prime_q, not_1_out;

  not not_1 (not_1_out, CLK);
  D_Flip_Flop #(.trigger("high")) DLATCH__E___CLK (.clk(D), .D(CLK), .Q(Q1));  // open: Qn, preset, en, reset
  D_Flip_Flop D_Flip_Flop__Rising_Edge (.clk(D), .D(CLK), .Q(Q2));  // open: Qn, preset, en, reset
  D_Flip_Flop #(.trigger("high")) DFF_MS__master__E___CLK_prime (
    .clk(D), .D(not_1_out), .Q(DFF_MS__master__E___CLK_prime_q));  // open: Qn, preset, en, reset
  D_Flip_Flop #(.trigger("high")) DLATCH_tang_1 (.clk(D), .D(CLK), .Q(L1));  // open: Qn, preset, en, reset
  D_Flip_Flop D_Flip_Flop_tang_1 (.clk(D), .D(CLK), .Q(F1));  // open: Qn, preset, en, reset
  D_Flip_Flop #(.trigger("high")) DFF_MS__slave__E___CLK (
    .clk(DFF_MS__master__E___CLK_prime_q), .D(CLK), .Q(Q3));  // open: Qn, preset, en, reset
  D_Flip_Flop #(.trigger("high")) DLATCH_tang_2 (.clk(L1), .D(CLK), .Q(L2));  // open: Qn, preset, en, reset
  D_Flip_Flop D_Flip_Flop_tang_2 (.clk(F1), .D(CLK), .Q(F2));  // open: Qn, preset, en, reset

  // Notes on the sheet:
  //   Latch vs Flip-Flop: so sanh Q1, Q2, Q3, L1/L2, F1/F2
  //   Chuoi 2 latch (cung E = CLK)
  //   Chuoi 2 flip-flop (cung CLK)
  //   DFF_MS = 2 DLATCH: master E = CLK', slave E = CLK
endmodule

module REGFILE (
  input  CLK,
  input  WE,
  input  [1:0] RD,
  input  [7:0] DIN,
  input  [1:0] RA,
  input  [1:0] RB,
  output [7:0] R0,
  output [7:0] QA,
  output [7:0] R1,
  output [7:0] R2,
  output [7:0] QB,
  output [7:0] R3
);

  wire and_3_out, and_4_out, decoder_1_out1, decoder_1_out2, decoder_1_out3;
  wire [7:0] undriven, undriven_2, undriven_3;

  Decoder #(.select(2), .enable("false")) decoder_1 (
    .out0(WE), .out1(decoder_1_out1), .out2(decoder_1_out2), .out3(decoder_1_out3), .sel(RD));
  and and_1 (DIN[0], WE, WE);
  and and_2 (DIN[0], decoder_1_out1, WE);
  and and_3 (and_3_out, decoder_1_out2, WE);
  and and_4 (and_4_out, decoder_1_out3, WE);
  Register register_1 (.D(undriven), .en(DIN[0]), .Q(R0), .clk(CLK));  // open: clr
  Register register_2 (.D(undriven), .en(DIN[0]), .Q(R1), .clk(CLK));  // open: clr
  Register register_3 (.D(undriven), .en(and_3_out), .Q(R2), .clk(CLK));  // open: clr
  Register register_4 (.D(undriven), .en(and_4_out), .Q(R3), .clk(CLK));  // open: clr
  Multiplexer #(.select(2), .width(8), .enable("false")) multiplexer_1 (
    .in0(R0), .in1(undriven_2), .in2(undriven_3), .in3(R3), .out(QA), .sel(RA));
  Multiplexer #(.select(2), .width(8), .enable("false")) multiplexer_2 (
    .in0(R0), .in1(undriven_2), .in2(undriven_3), .in3(R3), .out(QB), .sel(RA));
  // Pins of 1 and 8 bits meet at DIN

  assign RB = RA;
endmodule

module DATAPATH (
  input  [7:0] IMM,
  input  SRC,
  input  [2:0] OP,
  input  [1:0] RA,
  input  [1:0] RB,
  input  [1:0] RD,
  input  WE,
  input  CLK,
  output [7:0] R0,
  output [7:0] R1,
  output [7:0] R2,
  output [7:0] R3,
  output [7:0] R,
  output Z
);

  wire [7:0] multiplexer_1_out, regfile_1_qa, regfile_1_r0;

  Multiplexer #(.width(8), .enable("false")) multiplexer_1 (.in0(R), .in1(IMM), .out(multiplexer_1_out), .sel(SRC));
  REGFILE regfile_1 (
    .CLK(CLK), .WE(WE), .RD(RA), .DIN(multiplexer_1_out), .RA(RA), .RB(RB), .R0(regfile_1_r0),
    .QA(regfile_1_qa), .R1(R0), .R2(R1), .QB({R2[7:3], OP}), .R3(R3));
  ALU8 alu8_1 (.A(regfile_1_r0), .B(regfile_1_qa), .OP(OP), .R(R), .Z(Z));  // open: LT
  // Pins of 3 and 8 bits meet at {R2[7:3], OP}

  assign R2[2:0] = OP;
  assign RD = RA;
endmodule
